# Fritzing sketch StorageRoomAlarm (saved by Fritzing 0.9.3b)

parts:
  MKRFox1 = Arduino MKR Fox 1200
  S1 = Reed switch [package=THT]
  VCC1 = Battery  # not connected

nets:
  N1: MKRFox1.0, S1.pin_2
  N2: MKRFox1.VCC, S1.pin_1
